# Fritzing sketch Sketch (saved by Fritzing 0.9.3b)
breadboards: 1

parts:
  Part1 = BME280 Breakout
  U1 = NodeMCU V3.0
  Q1 = Basic FET P-Channel [package="TO220 [THT]"]
  D2 = Rectifier Diode [part_number=1N4001 package="300 mil [THT]"]
  S1 = Toggle Switch [package=THT]
  VCC1 = Battery
  D3 = Rectifier Diode [part_number=1N4001 package="300 mil [THT]"]
  Part2 = LCD1602-I2C

nets:
  GND: Part1.GND, U1.GND, Q1.drain, S1.COM, VCC1.-, Part2.GND
  3.3V: Part1.3.3V, Q1.source, Part2.VCC
  N1: Part1.SDI/SDA, U1.D3, Part2.SDA
  N2: Part1.SCK/SCL, U1.D2, Part2.SCL
  N3: U1.D0, D2.cathode
  N4: U1.Vin, Q1.gate, VCC1.+
  N5: U1.RST, D2.anode, D3.anode
  N6: S1.L1, D3.cathode

custom parts:
  NodeMCU V3.0: ESP8266 based NodeMCU
  LCD1602-I2C: A standard character display, usually with 2x16 characters. Comes in many colors with LCM1602 IIC attached.
